// Logisim project przyklad_mikroprogramowanie.circ as structural Verilog: 1 circuit, main circuit main
module main (
  input  [3:0] A,
  input  [3:0] B,
  input  \S___ładowanie_argumentow ,
  input  S___Am___Bm,
  input  S___Az___Bz,
  input  S___Az_Bz_LUB_Am_Bm,
  input  S___zapisywanie_wyniku,
  input  S___reset
);

  wire Az_q, Bz_q, clock_1_out, multiplexer_2_out;
  wire [2:0] adder_1_out, Am_q, Bm_q, multiplexer_1_out, multiplexer_3_out, multiplexer_4_out,
       subtractor_1_out;

  Clock clock_1 (.out(clock_1_out));
  Multiplexer #(.width(3), .enable("false")) multiplexer_1 (
    .in0(Bm_q), .in1(Am_q), .out(multiplexer_1_out), .sel(S___Am___Bm));
  Register #(.width(1)) Az (.D(A[3]), .en(\S___ładowanie_argumentow ), .Q(Az_q), .clk(clock_1_out), .clr(S___reset));
  Subtractor #(.width(3)) subtractor_1 (
    .a(multiplexer_1_out), .b(multiplexer_3_out), .out(subtractor_1_out));  // open: bin, bout
  Multiplexer #(.enable("false")) multiplexer_2 (
    .in0(Bz_q), .in1(Az_q), .out(multiplexer_2_out), .sel(S___Az_Bz_LUB_Am_Bm));
  Register #(.width(3)) Am (.D(A[2:0]), .en(\S___ładowanie_argumentow ), .Q(Am_q), .clk(clock_1_out), .clr(S___reset));
  Multiplexer #(.width(3), .enable("false")) multiplexer_3 (
    .in0(Am_q), .in1(Bm_q), .out(multiplexer_3_out), .sel(S___Am___Bm));
  Register #(.width(1)) Wz (
    .D(multiplexer_2_out), .en(S___zapisywanie_wyniku), .clk(clock_1_out), .clr(S___reset));  // open: Q
  Multiplexer #(.width(3), .enable("false")) multiplexer_4 (
    .in0(subtractor_1_out), .in1(adder_1_out), .out(multiplexer_4_out), .sel(S___Az___Bz));
  Register #(.width(3)) Wm (
    .D(multiplexer_4_out), .en(S___zapisywanie_wyniku), .clk(clock_1_out), .clr(S___reset));  // open: Q
  Register #(.width(1)) Bz (.D(B[3]), .en(\S___ładowanie_argumentow ), .Q(Bz_q), .clk(clock_1_out), .clr(S___reset));
  Register #(.width(3)) Bm (.D(B[2:0]), .en(\S___ładowanie_argumentow ), .Q(Bm_q), .clk(clock_1_out), .clr(S___reset));
  Adder #(.width(3)) adder_1 (.a(Bm_q), .b(Am_q), .out(adder_1_out));  // open: cin, cout
endmodule
